// Logisim project zomr.circ as structural Verilog: 3 circuits, main circuit main
module main (
  input  pc,
  input  in_2,
  input  in_3,
  input  in_4,
  input  in_5,
  input  in_6,
  input  in_7,
  input  in_8,
  input  in_9,
  input  in_10,
  input  in_11
);

  wire AC_INC, AC_LD, ADD, ALU_eout, AND, AR_load, clock_1_out, D_2_q, d_ff_1_q, D_q, decoder_1_out0,
       decoder_1_out1, decoder_1_out2, decoder_1_out3, decoder_1_out4, decoder_1_out5, decoder_1_out6,
       decoder_2_out0, decoder_2_out1, decoder_2_out2, decoder_2_out3, decoder_2_out4, decoder_2_out5,
       decoder_2_out6, decoder_2_out7, DR_LD, IR_LD, lcu_1_s_clr, lcu_1_sc_clr, MR_LD, MR_WR, PC_INC, S_q,
       TRNF;
  wire [2:0] SC_q, Ss;
  wire [7:0] bit_extender_1_out, INPR_q;
  wire [11:0] AR_q, bit_extender_2_out, bit_extender_3_out, PC_q;
  wire [15:0] AC_q, ALU_ac_2, bit_extender_4_out, bit_extender_5_out, DR_q, IR, multiplexer_1_out, ram_1_data;

  D_Flip_Flop S (.clk(clock_1_out), .Q(S_q), .reset(D_q));  // open: D, Qn, preset, en
  D_Flip_Flop D (.clk(clock_1_out), .D(lcu_1_s_clr), .Q(D_q));  // open: Qn, preset, en, reset
  Counter #(.width(3), .max('h7)) SC (.count(S_q), .Q(SC_q), .clk(clock_1_out), .clr(D_2_q));  // open: load, D, carry
  D_Flip_Flop D_2 (.clk(clock_1_out), .D(lcu_1_sc_clr), .Q(D_2_q));  // open: Qn, preset, en, reset
  Clock clock_1 (.out(clock_1_out));
  Decoder #(.select(3), .enable("false")) decoder_1 (
    .out0(decoder_1_out0), .out1(decoder_1_out1), .out2(decoder_1_out2), .out3(decoder_1_out3),
    .out4(decoder_1_out4), .out5(decoder_1_out5), .out6(decoder_1_out6), .out7(decoder_1_out6), .sel(SC_q));
  Decoder #(.select(3), .enable("false")) decoder_2 (
    .out0(decoder_2_out0), .out1(decoder_2_out1), .out2(decoder_2_out2), .out3(decoder_2_out3),
    .out4(decoder_2_out4), .out5(decoder_2_out5), .out6(decoder_2_out6), .out7(decoder_2_out7),
    .sel(IR[14:12]));
  Bit_Extender #(.in_width(16), .out_width(8)) bit_extender_1 (.in(multiplexer_1_out), .out(bit_extender_1_out));
  LCU lcu_1 (
    .T0(decoder_1_out0), .T1(decoder_1_out1), .T2(decoder_1_out2), .T3(decoder_1_out3), .T4(decoder_1_out4),
    .T5(decoder_1_out5), .T6(decoder_1_out6), .T7(decoder_1_out6), .B0(IR[0]), .B1(IR[1]), .B2(IR[2]),
    .B3(IR[3]), .B4(IR[4]), .B5(IR[5]), .B6(IR[6]), .B7(IR[7]), .B8(IR[8]), .B9(IR[9]), .B10(IR[10]),
    .B11(IR[11]), .D0(decoder_2_out0), .D1(decoder_2_out1), .D2(decoder_2_out2), .D3(decoder_2_out3),
    .D4(decoder_2_out4), .D5(decoder_2_out5), .D6(decoder_2_out6), .D7(decoder_2_out7), .I(IR[15]),
    .AR_LD(AR_load), .IR_LD(IR_LD), .DR_LD(DR_LD), .AC_LD(AC_LD), .MR_WR(MR_WR), .PC_INC(PC_INC), .AND(AND),
    .ADD(ADD), .TRNSFR(TRNF), .AC_INC(AC_INC), .So(Ss[2]), .S1(Ss[1]), .S2(Ss[0]), .SC_CLR(lcu_1_sc_clr),
    .S_CLR(lcu_1_s_clr));
  ALU ALU (
    .AC(AC_q), .DR(DR_q), .INPR(INPR_q), .Ein(d_ff_1_q), .in_2(in_6), .in_3(in_5), .in_4(in_4), .in_5(in_3),
    .TRSFR(TRNF), .ADD(ADD), .AND(AND), .Eout(ALU_eout), .AC_2(ALU_ac_2));
  and and_1 (MR_LD, Ss[2], Ss[1], Ss[0]);
  Bit_Extender #(.in_width(16), .out_width(12)) bit_extender_2 (.in(multiplexer_1_out), .out(bit_extender_2_out));
  Bit_Extender #(.in_width(16), .out_width(12)) bit_extender_3 (.in(multiplexer_1_out), .out(bit_extender_3_out));
  D_Flip_Flop d_ff_1 (.clk(clock_1_out), .D(ALU_eout), .Q(d_ff_1_q));  // open: Qn, preset, en, reset
  Counter #(.width(12), .max('hfff)) AR (
    .load(AR_load), .D(bit_extender_2_out), .count(in_7), .Q(AR_q), .clk(clock_1_out));  // open: carry, clr
  Counter #(.width(12), .max('hfff)) u_PC (
    .load(pc), .D(bit_extender_3_out), .count(PC_INC), .Q(PC_q), .clk(clock_1_out));  // open: carry, clr
  Counter #(.width(16), .max('hffff)) DR (
    .load(DR_LD), .D(multiplexer_1_out), .count(in_8), .Q(DR_q), .clk(clock_1_out));  // open: carry, clr
  Counter #(.width(16), .max('hffff)) AC (
    .load(AC_LD), .D(ALU_ac_2), .count(AC_INC), .Q(AC_q), .clk(clock_1_out));  // open: carry, clr
  Register INPR (.en(in_9), .Q(INPR_q), .clk(clock_1_out));  // open: D, clr
  Counter #(.width(16), .max('hffff)) u_IR (
    .load(IR_LD), .D(multiplexer_1_out), .count(in_10), .Q(IR), .clk(clock_1_out));  // open: carry, clr
  Counter OUTR (.load(in_2), .D(bit_extender_1_out), .count(in_11), .clk(clock_1_out));  // open: Q, carry, clr
  RAM #(.addrWidth(12), .dataWidth(16), .bus("separate")) ram_1 (
    .addr(AR_q), .din(multiplexer_1_out), .data(ram_1_data), .str(MR_WR), .clk(clock_1_out), .ld(MR_LD));  // open: sel, clr
  assign bit_extender_4_out = {{4{1'b0}}, AR_q};  // Bit_Extender bit_extender_4
  assign bit_extender_5_out = {{4{1'b0}}, PC_q};  // Bit_Extender bit_extender_5
  Multiplexer #(.select(3), .width(16), .enable("false")) multiplexer_1 (
    .in1(bit_extender_4_out), .in2(bit_extender_5_out), .in3(DR_q), .in4(AC_q), .in5(IR), .in7(ram_1_data),
    .out(multiplexer_1_out), .sel(Ss));  // open: in0, in6
endmodule

module ALU (
  input  TRSFR,
  input  in_2,
  input  in_3,
  input  in_4,
  input  in_5,
  input  ADD,
  input  AND,
  input  [15:0] AC,
  input  [15:0] DR,
  input  [7:0] INPR,
  input  Ein,
  output [15:0] AC_2,
  output Eout
);

  wire adder_1_cout, not_2_out;
  wire [1:0] bit_extender_1_out, or_1_out;
  wire [2:0] priority_encoder_1_out;
  wire [15:0] adder_1_out, and_1_out, bit_extender_2_out, not_1_out;

  Priority_Encoder priority_encoder_1 (
    .in0(AND), .in1(ADD), .in2(TRSFR), .in3(in_5), .in4(in_4), .in5(in_3), .in6(in_2),
    .out(priority_encoder_1_out));  // open: in7, en_in, gs, en_out
  assign and_1_out = AC & DR;  // AND_Gate and_1, 16 bits wide
  assign bit_extender_1_out = {{1{ADD}}, ADD};  // Bit_Extender bit_extender_1
  Adder #(.width(16)) adder_1 (.a(AC), .b(DR), .out(adder_1_out), .cout(adder_1_cout));  // open: cin
  assign bit_extender_2_out = {{8{1'b0}}, INPR};  // Bit_Extender bit_extender_2
  Multiplexer #(.select(3), .width(16), .enable("false")) multiplexer_1 (
    .in0(and_1_out), .in1(adder_1_out), .in2(DR), .in3(bit_extender_2_out), .in4(not_1_out),
    .in5({Ein, AC[15:1]}), .in6({AC[14:0], Ein}), .out(AC_2), .sel(priority_encoder_1_out));  // open: in7
  assign not_1_out = ~AC;  // NOT_Gate not_1, 16 bits wide
  assign or_1_out = bit_extender_1_out | {in_2, in_3};  // OR_Gate or_1, 2 bits wide
  Multiplexer #(.select(2), .disabled(0), .enable("false")) multiplexer_2 (
    .in0(not_2_out), .in1(AC[0]), .in2(AC[15]), .in3(adder_1_cout), .out(Eout), .sel(or_1_out));
  not not_2 (not_2_out, 1'b1);
endmodule

module LCU (
  input  T0,
  input  T1,
  input  T2,
  input  T3,
  input  T4,
  input  T5,
  input  T6,
  input  T7,
  input  B0,
  input  B1,
  input  B2,
  input  B3,
  input  B4,
  input  B5,
  input  B6,
  input  B7,
  input  B8,
  input  B9,
  input  B10,
  input  B11,
  input  D0,
  input  D1,
  input  D2,
  input  D3,
  input  D4,
  input  D5,
  input  D6,
  input  D7,
  input  I,
  output AR_LD,
  output IR_LD,
  output DR_LD,
  output AC_LD,
  output MR_WR,
  output PC_INC,
  output AND,
  output ADD,
  output TRNSFR,
  output AC_INC,
  output So,
  output S1,
  output S2,
  output SC_CLR,
  output S_CLR
);

  wire and_1_out, and_3_out, and_6_out, and_13_out, D0_D1_D2, MR_RD, not_1_out, or_5_out, r;

  not not_1 (not_1_out, I);
  and and_1 (and_1_out, T5, D0_D1_D2);
  or or_1 (D0_D1_D2, D0, D1, D2);
  and and_2 (r, D7, not_1_out, T3);
  and and_3 (and_3_out, D3, T4);
  and and_4 (AC_INC, B5, r);
  and and_5 (S_CLR, B0, r);
  or or_2 (SC_CLR, and_1_out, AC_INC, and_3_out);
  and and_6 (and_6_out, T4, D0_D1_D2);
  or or_3 (AR_LD, T0, T2);
  and and_7 (DR_LD, T4, D0_D1_D2);
  and and_8 (AC_LD, D0_D1_D2, T5);
  and and_9 (MR_WR, T4, D3);
  or or_4 (MR_RD, T1, and_6_out);
  and and_10 (AND, T5, D0);
  and and_11 (ADD, D1, T5);
  and and_12 (TRNSFR, T5, D2);
  or or_5 (or_5_out, D3, D0_D1_D2);
  and and_13 (and_13_out, T4, or_5_out);
  or or_6 (So, T2, T1, and_13_out);
  or or_7 (S1, MR_RD, T0);
  or or_8 (S2, MR_RD, T2);

  assign IR_LD = T1;
  assign PC_INC = T1;
endmodule
